# Fritzing sketch circuit (saved by Fritzing 0.9.3b)
breadboards: 1

parts:
  MCU1 = Raspberry Pi Zero
  NEOPIXEL1 = Neopixel Strip -- Black (30/m) [part_number=1376]
  Power_plug1 = Power plug
  U1 = 74AHCT125 [part_number=SN74AHCT125 package=dil14]

nets:
  GND: MCU1.pin_9, MCU1.pin_14, NEOPIXEL1.GND, Power_plug1.GND, U1.1OE, U1.GND
  N1: MCU1.pin_12, U1.1A
  N2: NEOPIXEL1.Din, U1.1Y
  VCC: NEOPIXEL1.+5V, Power_plug1.VCC, U1.VCC

custom parts:
  Neopixel Strip -- Black (30/m): These NeoPixel strips have 30 digitally-addressable pixel LEDs per meter and are very affordable and are only 12.5 mm wide, 10 mm if you remove the strip from the casing.
  74AHCT125: Quad Level-Shifter (3V to 5V) Quadruple Bus Buffer Gates With 3-State Outputs
